# Fritzing sketch HVP_Uno (saved by Fritzing 1.0.4)
breadboards: 1

parts:
  U2 = atmega328 [package=dip]
  FQP27P06 = Basic FET P-Channel [package="TO220 [THT]"]
  C2 = Ceramic Capacitor [capacitance=100nF voltage=35V package="100 mil [THT, multilayer]"]
  R1 = Resistor [tolerance=±5% resistance=22k package="1206 [SMD]"]
  R2 = Resistor [tolerance=±5% resistance=1k power=0.25W package=THT]
  12_Volt = Power plug
  C3 = Ceramic Capacitor [capacitance=10nF voltage=35V package="100 mil [THT, multilayer]"]
  R5 = Resistor [tolerance=±5% resistance=1k power=0.25W package=THT]
  R6 = Resistor [tolerance=±5% resistance=1k power=0.25W package=THT]
  R7 = Resistor [tolerance=±5% resistance=1k power=0.25W package=THT]
  R8 = Resistor [tolerance=±5% resistance=1k power=0.25W package=THT]
  R9 = Resistor [tolerance=±5% resistance=1k power=0.25W package=THT]
  R10 = Resistor [tolerance=±5% resistance=1k power=0.25W package=THT]
  R11 = Resistor [tolerance=±5% resistance=1k power=0.25W package=THT]
  R14 = Resistor [tolerance=±5% resistance=1k power=0.25W package=THT]
  R15 = Resistor [tolerance=±5% resistance=1k power=0.25W package=THT]
  R16 = Resistor [tolerance=±5% resistance=1k power=0.25W package=THT]
  R18 = Resistor [tolerance=±5% resistance=1k power=0.25W package=THT]
  R19 = Resistor [tolerance=±5% resistance=1k power=0.25W package=THT]
  R17 = Resistor [tolerance=±5% resistance=1k power=0.25W package=THT]
  J2 = female pin header, 4 pins [form="♀ (female)"]
  J3 = female pin header, 5 pins [form="♀ (female)"]
  J4 = female pin header, 3 pins [form="♀ (female)"]
  J1 = female pin header, 6 pins [form="♀ (female)"]
  J5 = female pin header, 6 pins [form="♀ (female)"]
  R3 = Resistor [tolerance=±5% power=0.25W resistance=1k package=THT]
  2N3904 = NPN-Transistor [package="TO92 [THT]"]
  J6 = female pin header, 6 pins [form="♀ (female)"]
  J7 = female pin header, 6 pins [form="♀ (female)"]
  Part1 = Arduino Uno (Rev3) - ICSP
  R4 = Resistor [tolerance=±5% resistance=1k power=0.25W package=THT]  # not connected
  R12 = Resistor [tolerance=±5% resistance=1k power=0.25W package=THT]  # not connected
  R20 = Resistor [tolerance=±5% resistance=1k power=0.25W package=THT]  # not connected
  R13 = Resistor [tolerance=±5% resistance=1k power=0.25W package=THT]  # not connected

nets (from the breadboard view):
  N1: U2.RESET, FQP27P06.drain
  N2: U2.D1_(TX), J2.pin4, J6.pin6, Part1.A0
  N3: U2.D2, R5.Pin_0, R5.Pin_1, J2.pin3, J6.pin5, Part1.A1
  N4: U2.D3_(PWM), R6.Pin_0, R6.Pin_1, J2.pin2, J6.pin4, Part1.A2
  N5: U2.D4, R7.Pin_0, R7.Pin_1, J2.pin1, J6.pin3, Part1.A3
  N6: U2.VCC, U2.AVCC, C2.0, R1.Pin_0, J5.pin4, Part1.D5_PWM
  GND: U2.GND, C2.1, 12_Volt.GND, C3.1, 2N3904.E, Part1.GND
  N7: U2.XLAT1, R8.Pin_0, R8.Pin_1, J1.pin6, J6.pin2, Part1.A4/SDA
  N8: U2.D5_(PWM), R9.Pin_0, R9.Pin_1, J1.pin4, J6.pin1, Part1.A5/SCL
  N9: U2.D6_(PWM), R10.Pin_0, R10.Pin_1, J1.pin3, J5.pin1, Part1.D2
  N10: U2.D7, R11.Pin_0, R11.Pin_1, J1.pin2, J5.pin2, Part1.D3_PWM
  N11: U2.D10_(PWM), R14.Pin_0, R14.Pin_1, J3.pin2, J7.pin1, Part1.D8
  N12: U2.D11_(PWM), R15.Pin_0, R15.Pin_1, J3.pin3, J7.pin2, Part1.D9_PWM
  N13: U2.D12, R16.Pin_0, R16.Pin_1, J3.pin4, J7.pin3, Part1.D10_PWM/SS
  N14: U2.D13, R17.Pin_0, R17.Pin_1, J3.pin5, J7.pin4, Part1.ICSP_MOSI, Part1.D11_PWM/MOSI
  N15: U2.A0, R18.Pin_0, R18.Pin_1, J4.pin1, J7.pin5, Part1.D12/MISO
  N16: U2.A1, R19.Pin_0, R19.Pin_1, J4.pin2, J7.pin6, Part1.D13/SCK
  N17: U2.A2, J4.pin3, J5.pin3, Part1.D4
  N18: FQP27P06.gate, R2.Pin_0, 2N3904.C
  N19: FQP27P06.source, R2.Pin_1, 12_Volt.VCC
  N20: R1.Pin_1, C3.0, R3.Pin_0
  N21: J3.pin1, J5.pin6, Part1.D7
  N22: J1.pin1, J5.pin5, Part1.D6_PWM
  N23: R3.Pin_1, 2N3904.B
